# Fritzing sketch hw setup (saved by Fritzing 0.9.8b)
breadboards: 1

parts:
  A1 = ESP32 38Pin narrow
  U1 = 74HC595 [package="DIP16 [THT]"]  # not connected
  U2 = 74HC595 [package="DIP16 [THT]"]  # not connected

nets:
  N1: A1.Pin_14, A1.Pin_32, A1.Pin_38

custom parts:
  ESP32 38Pin narrow: ESP32 38Pin narrow.
